// Logisim project comparators.circ as structural Verilog: 1 circuit, main circuit main
module main (
);

  wire and_1_out, and_2_out, and_3_out, and_4_out, and_5_out, and_6_out, and_7_out, and_8_out,
       comparator_1_eq, comparator_1_gt, comparator_1_lt, comparator_2_eq, comparator_2_gt, comparator_2_lt,
       comparator_3_eq, comparator_3_gt, comparator_3_lt, comparator_4_eq, comparator_4_gt, comparator_4_lt,
       comparator_5_eq, comparator_6_eq, or_1_out, or_2_out;

  Comparator #(.mode("unsigned"), .width(4)) comparator_1 (
    .a(4'b0000), .b(4'b0000), .gt(comparator_1_gt), .eq(comparator_1_eq), .lt(comparator_1_lt));
  Comparator #(.mode("unsigned"), .width(4)) comparator_2 (
    .a(4'b0000), .b(4'b0000), .gt(comparator_2_gt), .eq(comparator_2_eq), .lt(comparator_2_lt));
  Comparator #(.mode("unsigned"), .width(4)) comparator_3 (
    .a(4'b0000), .b(4'b0000), .gt(comparator_3_gt), .eq(comparator_3_eq), .lt(comparator_3_lt));
  Comparator #(.mode("unsigned"), .width(4)) comparator_4 (
    .a(4'b0000), .b(4'b0000), .gt(comparator_4_gt), .eq(comparator_4_eq), .lt(comparator_4_lt));
  Comparator #(.mode("unsigned"), .width(4)) comparator_5 (
    .a(4'b0001), .b(4'b0001), .eq(comparator_5_eq));  // open: gt, lt
  Comparator #(.mode("unsigned"), .width(4)) comparator_6 (
    .a(4'b0000), .b(4'b0000), .eq(comparator_6_eq));  // open: gt, lt
  and and_1 (and_1_out, comparator_1_gt, comparator_2_eq, comparator_3_eq, comparator_4_eq);
  and and_2 (and_2_out, comparator_2_gt, comparator_3_eq, comparator_4_eq);
  and and_3 (and_3_out, comparator_3_gt, comparator_4_eq);
  and and_4 (and_4_out, comparator_1_lt, comparator_2_eq, comparator_3_eq, comparator_4_eq);
  and and_5 (and_5_out, comparator_2_lt, comparator_3_eq, comparator_4_eq);
  and and_6 (and_6_out, comparator_3_lt, comparator_4_eq);
  and and_7 (and_7_out, comparator_5_eq, comparator_6_eq);
  or or_1 (or_1_out, and_1_out, and_2_out, and_3_out, comparator_4_gt);
  and and_8 (and_8_out, comparator_1_eq, comparator_2_eq, comparator_3_eq, comparator_4_eq);
  or or_2 (or_2_out, and_4_out, and_5_out, and_6_out, comparator_4_lt);

  // Notes on the sheet:
  //   A
  //   B
  //   A
  //   B
  //   16 bit comparator (=, <, >)
  //   7 bit comparator (=)
  //   A is equal to B
  //   A is greater than B
  //   A is equal to B
  //   A is smaller than B
endmodule
