// Logisim project organ16.circ as structural Verilog: 13 circuits, main circuit main
module main (
);

  wire clock_1_out, CLOCK_SIGNAL, cpu_1_halt, cpu_1_ram_clock, cpu_1_write_to_ram, gpu_1_screen_write_enable,
       IO_IN_OR_OUT, RESET, rgb_video_1_p2;
  wire [6:0] gpu_1_screen_x, gpu_1_screen_y;
  wire [15:0] cpu_1_ram_adress, cpu_1_ram_data_out, IO_DATA_OUT, IO_PORT_SELECT, io_ports_1_io_data_out,
       ram_module_1_ram_adress_out, ram_module_1_ram_data_out, ram_module_1_ram_written_data;

  IO_PORTS io_ports_1 (
    .RESET(RESET), .IO_PORT_SELECT(IO_PORT_SELECT), .IO_IN_OR_OUT(IO_IN_OR_OUT), .IO_DATA_IN(IO_DATA_OUT),
    .CLOCK_SIGNAL(CLOCK_SIGNAL), .IO_DATA_OUT(io_ports_1_io_data_out));
  Button RESET_SYSTEM (.out(RESET));
  CPU cpu_1 (
    .CLOCK_SIGNAL(CLOCK_SIGNAL), .GLOBAL_RESET(RESET), .IO_DATA_IN(io_ports_1_io_data_out),
    .RAM_DATA_IN(ram_module_1_ram_data_out), .IO_PORT(IO_PORT_SELECT), .IO_DATA_OUT(IO_DATA_OUT),
    .IO_IN_OUT(IO_IN_OR_OUT), .HALT(cpu_1_halt), .RAM_ADRESS(cpu_1_ram_adress),
    .WRITE_TO_RAM(cpu_1_write_to_ram), .RAM_CLOCK(cpu_1_ram_clock), .RAM_DATA_OUT(cpu_1_ram_data_out));
  CLOCK_MODULE clock_module_1 (.CLOCK_SIGNAL(clock_1_out), .HALT(cpu_1_halt), .OUTPUT_SIGNAL(CLOCK_SIGNAL));
  Clock clock_1 (.out(clock_1_out));
  RAM_MODULE ram_module_1 (
    .RESET(RESET), .WRITE_ENABLE(cpu_1_write_to_ram), .RAM_CLOCK(cpu_1_ram_clock),
    .RAM_DATA_IN(cpu_1_ram_data_out), .RAM_ADRESS_IN(cpu_1_ram_adress),
    .RAM_DATA_OUT(ram_module_1_ram_data_out), .RAM_ADRESS_OUT(ram_module_1_ram_adress_out),
    .RAM_WRITTEN_DATA(ram_module_1_ram_written_data));
  GPU gpu_1 (
    .RAM_ADRESS(ram_module_1_ram_adress_out), .SCREEN_WRITE_ENABLE(gpu_1_screen_write_enable),
    .SCREEN_X(gpu_1_screen_x), .SCREEN_Y(gpu_1_screen_y));
  // RGB_Video #(.cursor("No Cursor")) rgb_video_1: pin names not known; wires that end beside it: RESET, rgb_video_1_p2, gpu_1_screen_write_enable, gpu_1_screen_x, gpu_1_screen_y, ram_module_1_ram_written_data
  not not_1 (rgb_video_1_p2, CLOCK_SIGNAL);

  // Notes on the sheet:
  //   ORGAN-16 v2.5.0
endmodule

module CPU (
  input  [15:0] IO_DATA_IN,
  input  [15:0] RAM_DATA_IN,
  input  CLOCK_SIGNAL,
  input  GLOBAL_RESET,
  output HALT,
  output [15:0] IO_PORT,
  output [15:0] RAM_ADRESS,
  output [15:0] IO_DATA_OUT,
  output WRITE_TO_RAM,
  output IO_IN_OUT,
  output RAM_CLOCK,
  output [15:0] RAM_DATA_OUT
);

  wire ADDR_PHASE, and_5_out, and_6_out, and_7_out, and_12_out, and_15_out, and_16_out, and_17_out,
       and_18_out, and_20_out, and_21_out, and_22_out, and_23_out, and_24_out, ContainsAddress,
       CONTROL_UNIT_1_containsaddress, CONTROL_UNIT_1_isnextext, CONTROL_UNIT_1_jsr, CONTROL_UNIT_1_memwrite,
       CONTROL_UNIT_1_pc_load, CONTROL_UNIT_1_reg_is_adr, CONTROL_UNIT_1_regwrite, CONTROL_UNIT_1_sp_change,
       d_ff_1_q, ENABLE_ALU, FLAGS_WRITE, IO_ACCESS, IO_SPACE, IS_CURR_ADR, IS_CURR_ADR_BASE,
       IS_CURR_ADR_JSR, IS_CURR_EXT, IS_CURR_JSR, IS_CURR_RTS, IS_CURR_SP_CHANGE, IS_NEXT_EXT, JSR,
       MAIN_ALU_flag_carry, MAIN_ALU_flag_negative, MAIN_ALU_flag_overflow, MAIN_ALU_flag_zero, MEM_WRITE,
       multiplexer_10_out, multiplexer_14_out, multiplexer_17_out, NIO_ACCESS, not_2_out, not_3_out,
       not_4_out, not_5_out, not_6_out, not_7_out, not_8_out, not_9_out, not_10_out, not_11_out, not_12_out,
       not_13_out, not_14_out, not_15_out, not_16_out, not_17_out, not_18_out, not_19_out, not_20_out,
       not_21_out, not_22_out, not_23_out, not_24_out, not_25_out, not_26_out, not_27_out, not_28_out,
       or_1_out, or_2_out, or_3_out, or_4_out, or_6_out, or_7_out, or_11_out, PC_LOAD, POST_INC_FF, RAND_SEL,
       REG_IS_ADR, REG_IS_CURR_ADR, REG_WRITE, REG_WRITE_EFF, RTS, SP_CHANGE, SP_POP, USE_IN, WRITE_TO_RAM_t;
  wire [1:0] IO_MODE;
  wire [2:0] DST_EFF, DST_REG, SRC_REGA, SRC_REGB;
  wire [3:0] FLAGS;
  wire [4:0] ALU_OPCODE;
  wire [15:0] adder_1_out, adder_2_out, DATA_RB, demultiplexer_1_out0, demultiplexer_1_out1,
       INSTRUCTION_REG_MAIN_1_data_out, IR_EXT_DATA, MAIN_ALU_result, multiplexer_3_out, multiplexer_4_out,
       multiplexer_5_out, multiplexer_6_out, multiplexer_11_out, multiplexer_12_out, multiplexer_13_out,
       multiplexer_16_out, PROG_COUNTER, RAM_DATA_IN_t, register_1_q, STACK_POINTER, subtractor_1_out;

  not not_1 (NIO_ACCESS, IO_ACCESS);
  Multiplexer #(.width(16)) multiplexer_1 (.in0(RAM_DATA_IN), .in1(IO_DATA_IN), .out(RAM_DATA_IN_t), .sel(IO_ACCESS));
  and and_1 (IO_ACCESS, IO_SPACE, ADDR_PHASE);
  and and_2 (RAND_SEL, IO_MODE[0], IO_MODE[1]);
  and and_3 (WRITE_TO_RAM, WRITE_TO_RAM_t, NIO_ACCESS);
  Multiplexer #(.width(16)) multiplexer_2 (.in0(RAM_ADRESS), .in1(16'h1003), .out(IO_PORT), .sel(RAND_SEL));
  and and_4 (IO_IN_OUT, IO_ACCESS, WRITE_TO_RAM_t);
  Subtractor #(.width(16)) subtractor_1 (.a(STACK_POINTER), .b(16'h1), .out(subtractor_1_out));  // open: bin, bout
  Adder #(.width(16)) adder_1 (.a(STACK_POINTER), .b(16'h1), .out(adder_1_out));  // open: cin, cout
  not not_2 (not_2_out, CLOCK_SIGNAL);
  Demultiplexer #(.width(16)) demultiplexer_1 (
    .out0(demultiplexer_1_out0), .out1(demultiplexer_1_out1), .in(RAM_DATA_IN_t), .sel(IS_CURR_EXT));
  Multiplexer #(.width(16)) multiplexer_3 (
    .in0(subtractor_1_out), .in1(adder_1_out), .out(multiplexer_3_out), .sel(SP_POP));
  and and_5 (and_5_out, IS_CURR_SP_CHANGE, not_2_out);
  Register #(.width(16)) u_STACK_POINTER (
    .D(multiplexer_3_out), .en(1'b1), .clk(and_5_out), .Q(STACK_POINTER));  // open: clr
  // Probe on demultiplexer_1_out0
  // Probe on STACK_POINTER
  not not_3 (not_3_out, IS_CURR_SP_CHANGE);
  or or_1 (or_1_out, CLOCK_SIGNAL, IS_CURR_EXT, REG_IS_CURR_ADR);
  not not_4 (not_4_out, or_1_out);
  Register #(.width(16)) register_1 (.D(IR_EXT_DATA), .en(1'b1), .clk(not_5_out), .Q(register_1_q), .clr(GLOBAL_RESET));
  not not_5 (not_5_out, CLOCK_SIGNAL);
  INSTRUCTION_REG_MAIN INSTRUCTION_REG_MAIN_1 (
    .DATA_IN(demultiplexer_1_out0), .ENABLE(not_3_out), .CLOCK(not_4_out), .RESET(GLOBAL_RESET),
    .DATA_OUT(INSTRUCTION_REG_MAIN_1_data_out));
  INSTRUCTION_REG_EXT INSTRUCTION_REG_EXT_1 (
    .DATA_IN(demultiplexer_1_out1), .ENABLE(1'b1), .CLOCK(IS_CURR_EXT), .RESET(GLOBAL_RESET),
    .DATA_OUT(IR_EXT_DATA));
  // Probe on IR_EXT_DATA
  // Probe on INSTRUCTION_REG_MAIN_1_data_out
  // Probe on INSTRUCTION_REG_MAIN_1_data_out
  Multiplexer #(.width(16)) multiplexer_4 (
    .in0(DATA_RB), .in1(IR_EXT_DATA), .out(multiplexer_4_out), .sel(IS_CURR_EXT));
  Multiplexer #(.width(16)) multiplexer_5 (
    .in0(register_1_q), .in1(DATA_RB), .out(multiplexer_5_out), .sel(REG_IS_CURR_ADR));
  not not_6 (not_6_out, IS_CURR_JSR);
  not not_7 (not_7_out, PC_LOAD);
  not not_8 (not_8_out, IS_NEXT_EXT);
  Multiplexer #(.width(16)) multiplexer_6 (
    .in0(multiplexer_5_out), .in1(STACK_POINTER), .out(multiplexer_6_out), .sel(IS_CURR_SP_CHANGE));
  and and_6 (and_6_out, not_6_out, IS_CURR_ADR, IS_CURR_EXT, not_7_out);
  or or_2 (or_2_out, and_6_out, IS_CURR_SP_CHANGE, REG_IS_CURR_ADR);
  ALU MAIN_ALU (
    .A(IO_DATA_OUT), .B(multiplexer_4_out), .ALUOpCode(ALU_OPCODE), .ALU_Enable(ENABLE_ALU),
    .RESULT(MAIN_ALU_result), .FLAG_ZERO(MAIN_ALU_flag_zero), .FLAG_NEGATIVE(MAIN_ALU_flag_negative),
    .FLAG_CARRY(MAIN_ALU_flag_carry), .FLAG_OVERFLOW(MAIN_ALU_flag_overflow));
  and and_7 (and_7_out, FLAGS_WRITE, not_8_out);
  Multiplexer #(.width(16)) multiplexer_7 (
    .in0(PROG_COUNTER), .in1(multiplexer_6_out), .out(RAM_ADRESS), .sel(or_2_out));
  CONTROL_UNIT CONTROL_UNIT_1 (
    .OpCode(INSTRUCTION_REG_MAIN_1_data_out[15:13]), .SubOpCode(INSTRUCTION_REG_MAIN_1_data_out[12:9]),
    .OpData(INSTRUCTION_REG_MAIN_1_data_out[8:0]), .FLAGS(FLAGS), .ALU_Data({ENABLE_ALU, ALU_OPCODE}),
    .RegWrite(CONTROL_UNIT_1_regwrite), .SrcRB(SRC_REGB), .SrcRA(SRC_REGA), .DstR(DST_REG),
    .IsNextExt(CONTROL_UNIT_1_isnextext), .FlagsWrite(FLAGS_WRITE), .MemWrite(CONTROL_UNIT_1_memwrite),
    .ContainsAddress(CONTROL_UNIT_1_containsaddress), .PC_Load(CONTROL_UNIT_1_pc_load), .SP_POP(SP_POP),
    .SP_CHANGE(CONTROL_UNIT_1_sp_change), .JSR(CONTROL_UNIT_1_jsr), .RTS(RTS),
    .REG_IS_ADR(CONTROL_UNIT_1_reg_is_adr), .HALT(HALT), .USE_IN(USE_IN), .IO_SPACE(IO_SPACE),
    .IO_PORT(IO_MODE));
  Adder #(.width(16)) adder_2 (.a(PROG_COUNTER), .b(16'h2), .out(adder_2_out));  // open: cin, cout
  FLAGS_REG FLAGS_REG_1 (
    .IN_Z(MAIN_ALU_flag_zero), .IN_N(MAIN_ALU_flag_negative), .IN_C(MAIN_ALU_flag_carry),
    .IN_O(MAIN_ALU_flag_overflow), .ENABLE(and_7_out), .CLOCK(CLOCK_SIGNAL), .RESET(GLOBAL_RESET),
    .OUT_DATA(FLAGS));
  Multiplexer multiplexer_8 (.in0(CLOCK_SIGNAL), .in1(not_9_out), .out(RAM_CLOCK), .sel(IS_CURR_SP_CHANGE));
  not not_9 (not_9_out, CLOCK_SIGNAL);
  Multiplexer #(.width(16)) multiplexer_9 (.in0(IO_DATA_OUT), .in1(adder_2_out), .out(RAM_DATA_OUT), .sel(IS_CURR_JSR));
  not not_10 (not_10_out, IS_CURR_JSR);
  and and_8 (JSR, CONTROL_UNIT_1_jsr, not_10_out);
  Multiplexer multiplexer_10 (.in0(and_16_out), .in1(1'b0), .out(multiplexer_10_out), .sel(IS_CURR_EXT));
  not not_11 (not_11_out, CLOCK_SIGNAL);
  not not_12 (not_12_out, IS_CURR_EXT);
  and and_9 (REG_IS_ADR, CONTROL_UNIT_1_reg_is_adr, not_13_out);
  not not_13 (not_13_out, REG_IS_CURR_ADR);
  D_Flip_Flop d_ff_1 (
    .D(multiplexer_10_out), .clk(not_11_out), .Q(d_ff_1_q), .reset(GLOBAL_RESET));  // open: Qn, preset
  or or_3 (or_3_out, IS_CURR_EXT, ENABLE_ALU, REG_IS_CURR_ADR, USE_IN);
  and and_10 (IS_NEXT_EXT, CONTROL_UNIT_1_isnextext, not_12_out);
  not not_14 (not_14_out, IS_CURR_SP_CHANGE);
  not not_15 (not_15_out, IS_CURR_EXT);
  or or_4 (or_4_out, MEM_WRITE, IS_CURR_JSR);
  and and_11 (REG_WRITE, CONTROL_UNIT_1_regwrite, or_3_out);
  and and_12 (and_12_out, CONTROL_UNIT_1_containsaddress, IS_CURR_EXT);
  and and_13 (SP_CHANGE, CONTROL_UNIT_1_sp_change, not_14_out, not_15_out);
  Multiplexer #(.enable("true"), .width(16)) multiplexer_11 (
    .in0(MAIN_ALU_result), .in1(IR_EXT_DATA), .out(multiplexer_11_out), .sel(IS_CURR_EXT), .en(REG_WRITE_EFF));
  or or_5 (ContainsAddress, JSR, and_12_out);
  not not_16 (not_16_out, REG_WRITE);
  not not_17 (not_17_out, d_ff_1_q);
  or or_6 (or_6_out, IS_CURR_SP_CHANGE, REG_IS_CURR_ADR);
  or or_7 (or_7_out, IS_CURR_EXT, REG_IS_CURR_ADR);
  and and_14 (PC_LOAD, CONTROL_UNIT_1_pc_load, IS_CURR_EXT);
  and and_15 (and_15_out, REG_IS_CURR_ADR, not_16_out);
  and and_16 (and_16_out, or_4_out, not_17_out);
  Multiplexer #(.width(16)) multiplexer_12 (
    .in0(multiplexer_11_out), .in1(RAM_DATA_IN_t), .out(multiplexer_12_out), .sel(or_6_out));
  not not_18 (not_18_out, SP_POP);
  and and_17 (and_17_out, CONTROL_UNIT_1_memwrite, or_7_out);
  // Probe on RAM_DATA_IN
  or or_8 (WRITE_TO_RAM_t, and_15_out, and_16_out);
  Multiplexer #(.width(16)) multiplexer_13 (
    .in0(multiplexer_12_out), .in1(IO_DATA_IN), .out(multiplexer_13_out), .sel(USE_IN));
  and and_18 (and_18_out, IS_CURR_SP_CHANGE, not_18_out);
  or or_9 (MEM_WRITE, and_18_out, and_17_out);
  not not_19 (not_19_out, IS_CURR_JSR);
  Multiplexer multiplexer_14 (.in0(CLOCK_SIGNAL), .in1(not_20_out), .out(multiplexer_14_out), .sel(ADDR_PHASE));
  not not_20 (not_20_out, CLOCK_SIGNAL);
  and and_19 (ADDR_PHASE, IS_CURR_ADR, IS_CURR_EXT);
  and and_20 (and_20_out, PC_LOAD, not_19_out, IS_CURR_ADR);
  Multiplexer #(.width(3)) multiplexer_15 (.in0(DST_REG), .in1(SRC_REGB), .out(DST_EFF), .sel(POST_INC_FF));
  or or_10 (REG_WRITE_EFF, REG_WRITE, POST_INC_FF);
  or or_11 (or_11_out, and_20_out, RTS);
  not not_21 (not_21_out, IS_CURR_JSR);
  not not_22 (not_22_out, IS_CURR_SP_CHANGE);
  not not_23 (not_23_out, SP_CHANGE);
  not not_24 (not_24_out, REG_IS_CURR_ADR);
  not not_25 (not_25_out, REG_IS_ADR);
  and and_21 (and_21_out, CLOCK_SIGNAL, not_21_out, not_22_out, not_23_out, not_24_out, not_25_out);
  not not_26 (not_26_out, JSR);
  D_Flip_Flop CURRENT_IS_ADDR_BASE (
    .D(and_22_out), .clk(not_27_out), .Q(IS_CURR_ADR_BASE), .reset(GLOBAL_RESET));  // open: Qn, preset
  and and_22 (and_22_out, ContainsAddress, not_26_out);
  not not_27 (not_27_out, CLOCK_SIGNAL);
  D_Flip_Flop CURRENT_IS_ADDR_JSR (
    .D(ContainsAddress), .clk(CLOCK_SIGNAL), .Q(IS_CURR_ADR_JSR), .reset(GLOBAL_RESET));  // open: Qn, preset
  not not_28 (not_28_out, IS_CURR_EXT);
  Multiplexer #(.width(16)) multiplexer_16 (
    .in0(IR_EXT_DATA), .in1(RAM_DATA_IN_t), .out(multiplexer_16_out), .sel(RTS));
  D_Flip_Flop CURRENT_IS_EXT (
    .D(multiplexer_17_out), .clk(CLOCK_SIGNAL), .Q(IS_CURR_EXT), .reset(GLOBAL_RESET));  // open: Qn, preset
  Multiplexer multiplexer_17 (.in0(IS_NEXT_EXT), .in1(1'b1), .out(multiplexer_17_out), .sel(IS_CURR_JSR));
  D_Flip_Flop CURRENT_CHANGES_SP (
    .D(SP_CHANGE), .clk(CLOCK_SIGNAL), .Q(IS_CURR_SP_CHANGE), .reset(GLOBAL_RESET));  // open: Qn, preset
  D_Flip_Flop CURRENTLY_JSR (
    .D(and_23_out), .clk(CLOCK_SIGNAL), .Q(IS_CURR_JSR), .reset(GLOBAL_RESET));  // open: Qn, preset
  and and_23 (and_23_out, JSR, not_28_out);
  D_Flip_Flop CURRENTLY_RTS (.D(RTS), .clk(CLOCK_SIGNAL), .Q(IS_CURR_RTS), .reset(GLOBAL_RESET));  // open: Qn, preset
  D_Flip_Flop REG_IS_CURR_ADDR (
    .D(REG_IS_ADR), .clk(CLOCK_SIGNAL), .Q(REG_IS_CURR_ADR), .reset(GLOBAL_RESET));  // open: Qn, preset
  D_Flip_Flop u_POST_INC_FF (
    .D(and_24_out), .clk(CLOCK_SIGNAL), .Q(POST_INC_FF), .reset(GLOBAL_RESET));  // open: Qn, preset
  and and_24 (and_24_out, ENABLE_ALU, REG_IS_CURR_ADR);
  GENERAL_PURPOSE_REGS GENERAL_PURPOSE_REGS_1 (
    .RB_OUT(SRC_REGB), .RA_OUT(SRC_REGA), .R_WRITE(REG_WRITE_EFF), .DATA(multiplexer_13_out),
    .CLOCK(multiplexer_14_out), .R_IN(DST_EFF), .RESET(GLOBAL_RESET), .DATA_RA_OUT(IO_DATA_OUT),
    .DATA_RB_OUT(DATA_RB));
  PROGRAM_COUNTER PROGRAM_COUNTER_MAIN (
    .PC_DATA(multiplexer_16_out), .PC_Load(or_11_out), .CLOCK(and_21_out), .RESET(GLOBAL_RESET),
    .PC_Out(PROG_COUNTER));
  or or_12 (IS_CURR_ADR, IS_CURR_ADR_BASE, IS_CURR_ADR_JSR);
  // Probe on PROG_COUNTER

  // Other names for the same wires on the sheet: DATA_RA[15:0] = IO_DATA_OUT; IO_ADDR[15:0] = IO_PORT;
  //   IOM0 = IO_MODE[0]; IOM1 = IO_MODE[1]; IO_RD_DATA[15:0] = IO_DATA_IN; IO_WRITE = IO_IN_OUT;
  //   RAM_ADR_NET[15:0] = RAM_ADRESS; RAM_DATA_RAW[15:0] = RAM_DATA_IN; WRITE_TO_RAM_EXT = WRITE_TO_RAM

  // Notes on the sheet:
  //   IN / OUT = LOAD / STORE on the IO address space
  //   IO_ADDR = RAM_ADRESS (RAND forces 0x1003)
  //   OUT : IO_WRITE strobe, the RAM write is masked
  //   IN : IO data replaces RAM data (address phase)
  //   IO INTERFACE
  //   STACK POINTER
  //   INSTRUCTIONS REGs
  //   ALU + FLAGS REG
  //   MEMORY INTERFACE
  //   CONTROL UNIT
  //   GENERAL PURPOSE REGs
  //   PROGRAM COUNTER
  //   TEMPORARY VALUES
endmodule

module ALU (
  input  [15:0] A,
  input  [15:0] B,
  input  [4:0] ALUOpCode,
  input  ALU_Enable,
  output [15:0] RESULT,
  output FLAG_ZERO,
  output FLAG_NEGATIVE,
  output FLAG_CARRY,
  output FLAG_OVERFLOW
);

  wire A_GT_B, A_LT_B, adder_1_cout, and_2_out, and_3_out, B_IS_ZERO, B_LT16, nor_2_out, subtractor_1_bout,
       xnor_2_out, xor_2_out, xor_3_out, xor_4_out;
  wire [7:0] R_SQRT;
  wire [15:0] adder_1_out, adder_3_out, and_1_out, COS_OFF, DIV_RAW, divider_2_rem, multiplexer_15_out,
       multiplier_1_out, nand_1_out, NEG_A, nor_1_out, not_1_out, or_1_out, R_ABS, R_DIV, R_MAX, R_MIN,
       R_POW, R_SHL, R_SHR, R_SIN, R_TAN, R_XNOR, RES1, RES2, RES2A, SHL_RAW, SHR_RAW, SIN_ADDR,
       subtractor_1_out, subtractor_2_out, xor_1_out;

  ROM #(.addrWidth(16)) rom_1 (.addr(A), .data(R_SQRT));
  Multiplexer #(.width(16)) multiplexer_1 (.in0({16{1'b0}}), .in1(16'h4000), .out(COS_OFF), .sel(ALUOpCode[1]));
  Adder #(.width(16)) adder_1 (.a(A), .b(B), .out(adder_1_out), .cout(adder_1_cout));  // open: cin
  Subtractor #(.width(16)) subtractor_1 (.a(A), .b(B), .out(subtractor_1_out), .bout(subtractor_1_bout));  // open: bin
  Multiplier #(.width(16)) multiplier_1 (.a(A), .b(B), .out(multiplier_1_out));  // open: cin, cout
  Divider #(.width(16)) divider_1 (.a(A), .b(B), .out(DIV_RAW));  // open: upper, rem
  Divider #(.width(16)) divider_2 (.a(A), .b(B), .rem(divider_2_rem));  // open: out, upper
  assign and_1_out = A & B;  // AND_Gate and_1, 16 bits wide
  assign or_1_out = A | B;  // OR_Gate or_1, 16 bits wide
  assign nand_1_out = ~(A & B);  // NAND_Gate nand_1, 16 bits wide
  assign nor_1_out = ~(A | B);  // NOR_Gate nor_1, 16 bits wide
  assign xor_1_out = A ^ B;  // XOR_Gate xor_1, 16 bits wide
  Subtractor #(.width(16)) subtractor_2 (.a(A), .b(B), .out(subtractor_2_out));  // open: bin, bout
  assign not_1_out = ~A;  // NOT_Gate not_1, 16 bits wide
  assign R_XNOR = ~(A ^ B);  // XNOR_Gate xnor_1, 16 bits wide
  Comparator #(.mode("unsigned"), .width(16)) comparator_1 (.a(A), .b(B), .gt(A_GT_B), .lt(A_LT_B));  // open: eq
  Comparator #(.mode("unsigned"), .width(16)) comparator_2 (.a(B), .b({16{1'b0}}), .eq(B_IS_ZERO));  // open: gt, lt
  Comparator #(.width(12)) comparator_3 (.a(B[15:4]), .b({12{1'b0}}), .eq(B_LT16));  // open: gt, lt
  // Exponentiator #(.width(16)) exponentiator_1: pin names not known; wires that end beside it: A, B, R_POW
  Multiplexer #(.width(16)) multiplexer_2 (.in0(B), .in1(A), .out(R_MAX), .sel(A_GT_B));
  Adder #(.width(16)) adder_2 (.a(A), .b(COS_OFF), .out(SIN_ADDR));  // open: cin, cout
  Multiplexer #(.width(16)) multiplexer_3 (.in0(B), .in1(A), .out(R_MIN), .sel(A_LT_B));
  Multiplexer #(.width(16)) multiplexer_4 (.in0(DIV_RAW), .in1({16{1'b0}}), .out(R_DIV), .sel(B_IS_ZERO));
  ROM #(.addrWidth(16), .dataWidth(16)) rom_2 (.addr(SIN_ADDR), .data(R_SIN));
  Shifter #(.width(16)) shifter_1 (.in(A), .\dist (B[3:0]), .out(SHL_RAW));
  Shifter #(.shift("lr"), .width(16)) shifter_2 (.in(A), .\dist (B[3:0]), .out(SHR_RAW));
  Multiplexer #(.enable("true"), .select(4), .width(16)) multiplexer_5 (
    .in0(adder_1_out), .in1(subtractor_1_out), .in2(multiplier_1_out), .in3(R_DIV), .in4(divider_2_rem),
    .in5(and_1_out), .in6(or_1_out), .in7(nand_1_out), .in8(nor_1_out), .in9(xor_1_out),
    .in10(subtractor_2_out), .in11(not_1_out), .in12(R_XNOR), .in13(R_SHL), .in14(R_SHR), .in15(R_MIN),
    .out(RES1), .sel(ALUOpCode[3:0]), .en(ALU_Enable));
  Multiplexer #(.width(16)) multiplexer_6 (.in0(RES1), .in1(RES2), .out(RESULT), .sel(ALUOpCode[4]));
  Negator #(.width(16)) negator_1 (.in(A), .out(NEG_A));
  Multiplexer #(.enable("true"), .select(4)) multiplexer_7 (
    .in0(adder_1_cout), .in1(subtractor_1_bout), .in2(1'b0), .in3(1'b0), .in4(1'b0), .in5(1'b0), .in6(1'b0),
    .in7(1'b0), .in8(1'b0), .in9(1'b0), .in10(subtractor_1_bout), .out(FLAG_CARRY), .sel(ALUOpCode[3:0]),
    .en(ALU_Enable));  // open: in11, in12, in13, in14, in15
  Multiplexer #(.width(16)) multiplexer_8 (.in0({16{1'b0}}), .in1(SHL_RAW), .out(R_SHL), .sel(B_LT16));
  Multiplexer #(.width(16)) multiplexer_9 (.in0({16{1'b0}}), .in1(SHR_RAW), .out(R_SHR), .sel(B_LT16));
  nor nor_2 (nor_2_out, RESULT[0], RESULT[1], RESULT[2], RESULT[3], RESULT[4], RESULT[5], RESULT[6], RESULT[7], RESULT[8], RESULT[9], RESULT[10], RESULT[11], RESULT[12], RESULT[13], RESULT[14], RESULT[15]);
  ROM #(.addrWidth(16), .dataWidth(16)) rom_3 (.addr(A), .data(R_TAN));
  xor xor_2 (xor_2_out, RESULT[15], A[15]);
  xnor xnor_2 (xnor_2_out, A[15], B[15]);
  xor xor_3 (xor_3_out, RESULT[15], A[15]);
  xor xor_4 (xor_4_out, A[15], B[15]);
  Multiplexer #(.width(16)) multiplexer_10 (.in0(A), .in1(NEG_A), .out(R_ABS), .sel(A[15]));
  and and_2 (and_2_out, xor_2_out, xnor_2_out);
  and and_3 (and_3_out, xor_3_out, xor_4_out);
  Multiplexer multiplexer_11 (.in0(1'b0), .in1(nor_2_out), .out(FLAG_ZERO), .sel(ALU_Enable));
  Multiplexer #(.select(3), .width(16)) multiplexer_12 (
    .in0(R_MAX), .in1(R_SIN), .in2(R_SIN), .in3(R_TAN), .in4({{8{1'b0}}, R_SQRT}), .in5(R_POW), .in6(R_ABS),
    .in7(A), .out(RES2A), .sel(ALUOpCode[2:0]));
  Multiplexer multiplexer_13 (.in0(1'b0), .in1(RESULT[15]), .out(FLAG_NEGATIVE), .sel(ALU_Enable));
  Multiplexer #(.enable("true"), .select(4)) multiplexer_14 (
    .in0(and_2_out), .in1(and_3_out), .in2(1'b0), .in3(1'b0), .in4(1'b0), .in5(1'b0), .in6(1'b0), .in7(1'b0),
    .in8(1'b0), .in9(1'b0), .in10(and_3_out), .out(FLAG_OVERFLOW), .sel(ALUOpCode[3:0]), .en(ALU_Enable));  // open: in11, in12, in13, in14, in15
  Multiplexer #(.width(16)) multiplexer_15 (
    .in0(16'h1), .in1({16{1'b1}}), .out(multiplexer_15_out), .sel(ALUOpCode[1]));
  Adder #(.width(16)) adder_3 (.a(B), .b(multiplexer_15_out), .out(adder_3_out));  // open: cin, cout
  Multiplexer #(.width(16)) multiplexer_16 (.in0(RES2A), .in1(adder_3_out), .out(RES2), .sel(ALUOpCode[3]));

  // Other names for the same wires on the sheet: A_B15 = A[15]; OP_B4 = ALUOpCode[4]; B_LOW4[3:0] = B[3:0];
  //   B_HIGH12[11:0] = B[15:4]; OP3[2:0] = ALUOpCode[2:0]; OP4[3:0] = ALUOpCode[3:0]; OP_B1 = ALUOpCode[1];
  //   OP_B3 = ALUOpCode[3]; SQRT8[7:0] = R_SQRT

  // Notes on the sheet:
  //   ADD
  //   SUB
  //   MUL
  //   DIV
  //   MOD
  //   AND
  //   OR
  //   NAND
  //   NOR
  //   XOR
  //   CMP
  //   NOT
  //   contents of rom_1 (hex, n*v repeats v):
  //   0 1 1 1 5*2 7*3 9*4 11*5 13*6 15*7 17*8 19*9 21*a 23*b 25*c 27*d 29*e 31*f 33*10 35*11 37*12 39*13
  //   41*14 43*15 45*16 47*17 49*18 51*19 53*1a 55*1b 57*1c 59*1d 61*1e 63*1f 65*20 67*21 69*22 71*23
  //   73*24 75*25 77*26 79*27 81*28 83*29 85*2a 87*2b 89*2c 91*2d 93*2e 95*2f 97*30 99*31 101*32 103*33
  //   105*34 107*35 109*36 111*37 113*38 115*39 117*3a 119*3b 121*3c 123*3d 125*3e 127*3f 129*40 131*41
  //   133*42 135*43 137*44 139*45 141*46 143*47 145*48 147*49 149*4a 151*4b 153*4c 155*4d 157*4e 159*4f
  //   161*50 163*51 165*52 167*53 169*54 171*55 173*56 175*57 177*58 179*59 181*5a 183*5b 185*5c 187*5d
  //   189*5e 191*5f 193*60 195*61 197*62 199*63 201*64 203*65 205*66 207*67 209*68 211*69 213*6a 215*6b
  //   217*6c 219*6d 221*6e 223*6f 225*70 227*71 229*72 231*73 233*74 235*75 237*76 239*77 241*78 243*79
  //   245*7a 247*7b 249*7c 251*7d 253*7e 255*7f 257*80 259*81 261*82 263*83 265*84 267*85 269*86 271*87
  //   273*88 275*89 277*8a 279*8b 281*8c 283*8d 285*8e 287*8f 289*90 291*91 293*92 295*93 297*94 299*95
  //   301*96 303*97 305*98 307*99 309*9a 311*9b 313*9c 315*9d 317*9e 319*9f 321*a0 323*a1 325*a2 327*a3
  //   329*a4 331*a5 333*a6 335*a7 337*a8 339*a9 341*aa 343*ab 345*ac 347*ad 349*ae 351*af 353*b0 355*b1
  //   357*b2 359*b3 361*b4 363*b5 365*b6 367*b7 369*b8 371*b9 373*ba 375*bb 377*bc 379*bd 381*be 383*bf
  //   385*c0 387*c1 389*c2 391*c3 393*c4 395*c5 397*c6 399*c7 401*c8 403*c9 405*ca 407*cb 409*cc 411*cd
  //   413*ce 415*cf 417*d0 419*d1 421*d2 423*d3 425*d4 427*d5 429*d6 431*d7 433*d8 435*d9 437*da 439*db
  //   441*dc 443*dd 445*de 447*df 449*e0 451*e1 453*e2 455*e3 457*e4 459*e5 461*e6 463*e7 465*e8 467*e9
  //   469*ea 471*eb 473*ec 475*ed 477*ee 479*ef 481*f0 483*f1 485*f2 487*f3 489*f4 491*f5 493*f6 495*f7
  //   497*f8 499*f9 501*fa 503*fb 505*fc 507*fd 509*fe 511*ff
  //   DIV : division by 0 gives 0
  //   SHL / SHR (logical, amount >= 16 gives 0)
  //   MIN / MAX (unsigned)
  //   POW (A ** B)
  //   SQRT (ROM, floor of the square root)
  //   SIN / COS (ROM, COS = SIN at A + 0x4000), Q1.15
  //   XNOR / SHL / SHR / MIN feed the main multiplexer (ALUOpCode 12-15)
  //   contents of rom_2 (hex, n*v repeats v):
  //   0 3 6 9 d 10 13 16 19 1c 1f 23 26 29 2c 2f 32 35 39 3c 3f 42 45 48 4b 4f 52 55 58 5b 5e 61 65 68 6b
  //   6e 71 74 77 7b 7e 81 84 87 8a 8d 91 94 97 9a 9d a0 a3 a6 aa ad b0 b3 b6 b9 bc c0 c3 c6 c9 cc cf d2
  //   d6 d9 dc df e2 e5 e8 ec ef f2 f5 f8 fb fe 102 105 108 10b 10e 111 114 118 11b 11e 121 124 127 12a
  //   12e 131 134 137 13a 13d 140 144 147 14a 14d 150 153 156 15a 15d 160 163 166 169 16c 170 173 176 179
  //   17c 17f 182 186 189 18c 18f 192 195 198 19c 19f 1a2 1a5 1a8 1ab 1ae 1b2 1b5 1b8 1bb 1be 1c1 1c4 1c8
  //   1cb 1ce 1d1 1d4 1d7 1da 1dd 1e1 1e4 1e7 1ea 1ed 1f0 1f3 1f7 1fa 1fd 200 203 206 209 20d 210 213 216
  //   219 21c 21f 223 226 229 22c 22f 232 235 239 23c 23f 242 245 248 24b 24f 252 255 258 25b 25e 261 265
  //   268 26b 26e 271 274 277 27b 27e 281 284 287 28a 28d 291 294 297 29a 29d 2a0 2a3 2a7 2aa 2ad 2b0 2b3
  //   2b6 2b9 2bd 2c0 2c3 2c6 2c9 2cc 2cf 2d2 2d6 2d9 2dc 2df 2e2 2e5 2e8 2ec 2ef 2f2 2f5 2f8 2fb 2fe 302
  //   305 308 30b 30e 311 314 318 31b 31e 321 324 327 32a 32e 331 334 337 33a 33d 340 344 347 34a 34d 350
  //   353 356 35a 35d 360 363 366 369 36c 370 373 376 379 37c 37f 382 385 389 38c 38f 392 395 398 39b 39f
  //   3a2 3a5 3a8 3ab 3ae 3b1 3b5 3b8 3bb 3be 3c1 3c4 3c7 3cb 3ce 3d1 3d4 3d7 3da 3dd 3e1 3e4 3e7 3ea 3ed
  //   3f0 3f3 3f7 3fa 3fd 400 403 406 409 40d 410 413 416 419 41c 41f 423 426 429 42c 42f 432 435 438 43c
  //   43f 442 445 448 44b 44e 452 455 458 45b 45e 461 464 468 46b 46e 471 474 477 47a 47e 481 484 487 48a
  //   48d 490 494 497 49a 49d 4a0 4a3 4a6 4aa 4ad 4b0 4b3 4b6 4b9 4bc 4bf 4c3 4c6 4c9 4cc 4cf 4d2 4d5 4d9
  //   4dc 4df 4e2 4e5 4e8 4eb 4ef 4f2 4f5 4f8 4fb 4fe 501 505 508 50b 50e 511 514 517 51b 51e 521 524 527
  //   52a 52d 530 534 537 53a 53d 540 543 546 54a 54d 550 553 556 559 55c 560 563 566 569 56c 56f 572 576
  //   579 57c 57f 582 585 588 58c 58f 592 595 598 59b 59e 5a1 5a5 5a8 5ab 5ae 5b1 5b4 5b7 5bb 5be 5c1 5c4
  //   5c7 5ca 5cd 5d1 5d4 5d7 5da 5dd 5e0 5e3 5e7 5ea 5ed 5f0 5f3 5f6 5f9 5fc 600 603 606 609 60c 60f 612
  //   616 619 61c 61f 622 625 628 62c 62f 632 635 638 63b 63e 642 645 648 64b 64e 651 654 657 65b 65e 661
  //   664 667 66a 66d 671 674 677 67a 67d 680 683 687 68a 68d 690 693 696 699 69d 6a0 6a3 6a6 6a9 6ac 6af
  //   6b2 6b6 6b9 6bc 6bf 6c2 6c5 6c8 6cc 6cf 6d2 6d5 6d8 6db 6de 6e2 6e5 6e8 6eb 6ee 6f1 6f4 6f7 6fb 6fe
  //   701 704 707 70a 70d 711 714 717 71a 71d 720 723 727 72a 72d 730 733 736 739 73c 740 743 746 749 74c
  //   74f 752 756 759 75c 75f 762 765 768 76c 76f 772 775 778 77b 77e 781 785 788 78b 78e 791 794 797 79b
  //   79e 7a1 7a4 7a7 7aa 7ad 7b1 7b4 7b7 7ba 7bd 7c0 7c3 7c6 7ca 7cd 7d0 7d3 7d6 7d9 7dc 7e0 7e3 7e6 7e9
  //   7ec 7ef 7f2 7f6 7f9 7fc 7ff 802 805 808 80b 80f 812 815 818 81b 81e 821 825 828 82b 82e 831 834 837
  //   83a 83e 841 844 847 84a 84d 850 854 857 85a 85d 860 863 866 86a 86d 870 873 876 879 87c 87f 883 886
  //   889 88c 88f 892 895 899 89c 89f 8a2 8a5 8a8 8ab 8ae 8b2 8b5 8b8 8bb 8be 8c1 8c4 8c8 8cb 8ce 8d1 8d4
  //   8d7 8da 8dd 8e1 8e4 8e7 8ea 8ed 8f0 8f3 8f7 8fa 8fd 900 903 906 909 90c 910 913 916 919 91c 91f 922
  //   926 929 92c 92f 932 935 938 93b 93f 942 945 948 94b 94e 951 955 958 95b 95e 961 964 967 96a 96e 971
  //   974 977 97a 97d 980 984 987 98a 98d 990 993 996 999 99d 9a0 9a3 9a6 9a9 9ac 9af 9b3 9b6 9b9 9bc 9bf
  //   9c2 9c5 9c8 9cc 9cf 9d2 9d5 9d8 9db 9de 9e2 9e5 9e8 9eb 9ee 9f1 9f4 9f7 9fb 9fe a01 a04 a07 a0a a0d
  //   a11 a14 a17 a1a a1d a20 a23 a26 a2a a2d a30 a33 a36 a39 a3c a3f a43 a46 a49 a4c a4f a52 a55 a59 a5c
  //   a5f a62 a65 a68 a6b a6e a72 a75 a78 a7b a7e a81 a84 a87 a8b a8e a91 a94 a97 a9a a9d aa1 aa4 aa7 aaa
  //   aad ab0 ab3 ab6 aba abd ac0 ac3 ac6 ac9 acc acf ad3 ad6 ad9 adc adf ae2 ae5 ae9 aec aef af2 af5 af8
  //   afb afe b02 b05 b08 b0b b0e b11 b14 b17 b1b b1e b21 b24 b27 b2a b2d b31 b34 b37 b3a b3d b40 b43 b46
  //   b4a b4d b50 b53 b56 b59 b5c b5f b63 b66 b69 b6c b6f b72 b75 b78 b7c b7f b82 b85 b88 b8b b8e b92 b95
  //   b98 b9b b9e ba1 ba4 ba7 bab bae bb1 bb4 bb7 bba bbd bc0 bc4 bc7 bca bcd bd0 bd3 bd6 bd9 bdd be0 be3
  //   be6 be9 bec bef bf3 bf6 bf9 bfc bff c02 c05 c08 c0c c0f c12 c15 c18 c1b c1e c21 c25 c28 c2b c2e c31
  //   c34 c37 c3a c3e c41 c44 c47 c4a c4d c50 c53 c57 c5a c5d c60 c63 c66 c69 c6c c70 c73 c76 c79 c7c c7f
  //   c82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
  //   ABS (signed)
  //   contents of rom_3 (hex, n*v repeats v):
  //   21*0 41*1 40*2 41*3 41*4 41*5 40*6 41*7 41*8 40*9 41*a 41*b 40*c 41*d 41*e 40*f 41*10 40*11 41*12
  //   40*13 41*14 40*15 41*16 40*17 41*18 40*19 40*1a 41*1b 40*1c 40*1d 40*1e 41*1f 40*20 40*21 40*22
  //   40*23 40*24 40*25 39*26 40*27 40*28 40*29 39*2a 40*2b 40*2c 39*2d 40*2e 39*2f 39*30 40*31 39*32
  //   39*33 39*34 39*35 39*36 39*37 39*38 39*39 39*3a 38*3b 39*3c 39*3d 38*3e 39*3f 38*40 38*41 38*42
  //   38*43 39*44 38*45 37*46 38*47 38*48 38*49 37*4a 38*4b 37*4c 38*4d 37*4e 37*4f 37*50 37*51 37*52
  //   37*53 37*54 37*55 36*56 37*57 36*58 37*59 36*5a 36*5b 36*5c 36*5d 36*5e 36*5f 35*60 36*61 36*62
  //   35*63 35*64 36*65 35*66 35*67 35*68 35*69 35*6a 34*6b 35*6c 34*6d 35*6e 34*6f 34*70 34*71 34*72
  //   34*73 34*74 34*75 33*76 34*77 33*78 34*79 33*7a 33*7b 33*7c 33*7d 33*7e 32*7f 33*80 32*81 33*82
  //   32*83 32*84 32*85 32*86 32*87 32*88 32*89 31*8a 32*8b 31*8c 31*8d 31*8e 31*8f 31*90 31*91 31*92
  //   31*93 30*94 31*95 30*96 30*97 30*98 30*99 30*9a 30*9b 30*9c 29*9d 30*9e 29*9f 30*a0 29*a1 29*a2
  //   29*a3 29*a4 28*a5 29*a6 29*a7 28*a8 29*a9 28*aa 28*ab 28*ac 28*ad 28*ae 28*af 27*b0 28*b1 27*b2
  //   28*b3 27*b4 27*b5 27*b6 27*b7 27*b8 27*b9 27*ba 26*bb 27*bc 26*bd 26*be 26*bf 26*c0 26*c1 26*c2
  //   26*c3 26*c4 25*c5 26*c6 25*c7 26*c8 25*c9 25*ca 25*cb 25*cc 25*cd 24*ce 25*cf 25*d0 24*d1 24*d2
  //   25*d3 24*d4 24*d5 24*d6 24*d7 24*d8 23*d9 24*da 23*db 24*dc 23*dd 23*de 24*df 23*e0 23*e1 23*e2
  //   22*e3 23*e4 23*e5 22*e6 23*e7 22*e8 22*e9 23*ea 22*eb 22*ec 22*ed 22*ee 21*ef 22*f0 22*f1 21*f2
  //   22*f3 21*f4 21*f5 21*f6 21*f7 21*f8 21*f9 21*fa 21*fb 21*fc 20*fd 21*fe 20*ff 21*100 20*101 20*102
  //   20*103 20*104 20*105 20*106 20*107 20*108 19*109 20*10a 20*10b 19*10c 19*10d 20*10e 19*10f 19*110
  //   19*111 19*112 19*113 19*114 19*115 18*116 19*117 18*118 19*119 18*11a 19*11b 18*11c 18*11d 18*11e
  //   18*11f 18*120 18*121 18*122 18*123 18*124 17*125 18*126 17*127 18*128 17*129 17*12a 18*12b 17*12c
  //   17*12d 17*12e 17*12f 17*130 17*131 16*132 17*133 17*134 16*135 17*136 16*137 17*138 16*139 16*13a
  //   17*13b 16*13c 16*13d 16*13e 16*13f 16*140 15*141 16*142 16*143 16*144 15*145 16*146 15*147 16*148
  //   15*149 15*14a 16*14b 15*14c 15*14d 15*14e 15*14f 15*150 15*151 15*152 15*153 14*154 15*155 15*156
  //   14*157 15*158 14*159 15*15a 14*15b 14*15c 15*15d 14*15e 14*15f 14*160 14*161 14*162 14*163 14*164
  //   14*165 13*166 14*167 14*168 13*169 14*16a 14*16b 13*16c 14*16d 13*16e 13*16f 14*170 13*171 13*172
  //   13*173 13*174 13*175 13*176 13*177 13*178 13*179 13*17a 13*17b 12*17c 13*17d 13*17e 12*17f 13*180
  //   12*181 13*182 12*183 12*184 13*185 12*186 12*187 12*188 12*189 13*18a 12*18b 12*18c 12*18d 12*18e
  //   11*18f 12*190 12*191 12*192 12*193 11*194 12*195 11*196 12*197 11*198 12*199 11*19a 12*19b 11*19c
  //   11*19d 12*19e 11*19f 11*1a0 11*1a1 11*1a2 11*1a3 11*1a4 11*1a5 11*1a6 11*1a7 11*1a8 11*1a9 11*1aa
  //   11*1ab 10*1ac 11*1ad 11*1ae 10*1af 11*1b0 11*1b1 10*1b2 11*1b3 10*1b4 10*1b5 11*1b6 10*1b7 10*1b8
  //   11*1b9 10*1ba 10*1bb 10*1bc 10*1bd 11*1be 10*1bf 10*1c0 10*1c1 10*1c2 10*1c3 9*1c4 10*1c5 10*1c6
  //   10*1c7 10*1c8 9*1c9 10*1ca 10*1cb 9*1cc 10*1cd 10*1ce 9*1cf 10*1d0 9*1d1 10*1d2 9*1d3 9*1d4 10*1d5
  //   9*1d6 9*1d7 10*1d8 9*1d9 9*1da 9*1db 9*1dc 9*1dd 9*1de 10*1df 9*1e0 9*1e1 9*1e2 8*1e3 9*1e4 9*1e5
  //   9*1e6 9*1e7 9*1e8 8*1e9 9*1ea 9*1eb 9*1ec 8*1ed 9*1ee 8*1ef 9*1f0 9*1f1 8*1f2 9*1f3 8*1f4 8*1f5
  //   9*1f6 8*1f7 9*1f8 8*1f9 8*1fa 9*1fb 8*1fc 8*1fd 8*1fe 8*1ff 9*200 8*201 8*202 8*203 8*204 8*205
  //   8*206 8*207 8*208 8*209 8*20a 8*20b 7*20c 8*20d 8*20e 8*20f 8*210 7*211 8*212 8*213 7*214 8*215
  //   8*216 7*217 8*218 7*219 8*21a 7*21b 8*21c 7*21d 8*21e 7*21f 7*220 8*221 7*222 7*223 8*224 7*225
  //   7*226 8*227 7*228 7*229 7*22a 7*22b 7*22c 8*22d 7*22e 7*22f 7*230 7*231 7*232 7*233 7*234 7*235
  //   7*236 6*237 7*238 7*239 7*23a 7*23b 7*23c 6*23d 7*23e 7*23f 7*240 6*241 7*242 7*243 6*244 7*245
  //   7*246 6*247 7*248 6*249 7*24a 6*24b 7*24c 6*24d 7*24e 6*24f 7*250 6*251 6*252 7*253 6*254 6*255
  //   7*256 6*257 6*258 7*259 6*25a 6*25b 6*25c 6*25d 7*25e 6*25f 6*260 6*261 6*262 6*263 6*264 6*265
  //   6*266 6*267 6*268 6*269 6*26a 6*26b 6*26c 6*26d 6*26e 6*26f 6*270 6*271 5*272 6*273 6*274 6*275
  //   6*276 5*277 6*278 6*279 6*2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
  //   ALUOpCode 16-23 : MAX SIN COS TAN SQRT POW ABS MOV
  //   TAN (ROM), Q8.8
endmodule

module CLOCK_MODULE (
  input  CLOCK_SIGNAL,
  input  HALT,
  output OUTPUT_SIGNAL
);

  wire not_1_out;

  not not_1 (not_1_out, HALT);
  and and_1 (OUTPUT_SIGNAL, CLOCK_SIGNAL, not_1_out);
endmodule

module GENERAL_PURPOSE_REGS (
  input  [15:0] DATA,
  input  R_WRITE,
  input  [2:0] R_IN,
  input  CLOCK,
  input  [2:0] RA_OUT,
  input  RESET,
  input  [2:0] RB_OUT,
  output [15:0] DATA_RA_OUT,
  output [15:0] DATA_RB_OUT
);

  wire decoder_1_out0, decoder_1_out1, decoder_1_out2, decoder_1_out3, decoder_1_out4, decoder_1_out5,
       decoder_1_out6, decoder_1_out7, not_1_out, not_2_out, not_3_out, not_4_out, not_5_out, not_6_out,
       not_7_out, not_8_out;
  wire [15:0] R0_q, R1_q, R2_q, R3_q, R4_q, R5_q, R6_q, R7_q;

  // Probe on DATA
  Decoder #(.select(3)) decoder_1 (
    .out0(decoder_1_out0), .out1(decoder_1_out1), .out2(decoder_1_out2), .out3(decoder_1_out3),
    .out4(decoder_1_out4), .out5(decoder_1_out5), .out6(decoder_1_out6), .out7(decoder_1_out7), .sel(R_IN),
    .en(R_WRITE));
  Register #(.width(16)) R0 (.D(DATA), .en(decoder_1_out0), .clk(not_1_out), .Q(R0_q), .clr(RESET));
  not not_1 (not_1_out, CLOCK);
  Register #(.width(16)) R1 (.D(DATA), .en(decoder_1_out1), .clk(not_2_out), .Q(R1_q), .clr(RESET));
  not not_2 (not_2_out, CLOCK);
  Register #(.width(16)) R2 (.D(DATA), .en(decoder_1_out2), .clk(not_3_out), .Q(R2_q), .clr(RESET));
  not not_3 (not_3_out, CLOCK);
  Register #(.width(16)) R3 (.D(DATA), .en(decoder_1_out3), .clk(not_4_out), .Q(R3_q), .clr(RESET));
  not not_4 (not_4_out, CLOCK);
  Register #(.width(16)) R4 (.D(DATA), .en(decoder_1_out4), .clk(not_5_out), .Q(R4_q), .clr(RESET));
  not not_5 (not_5_out, CLOCK);
  Register #(.width(16)) R5 (.D(DATA), .en(decoder_1_out5), .clk(not_6_out), .Q(R5_q), .clr(RESET));
  not not_6 (not_6_out, CLOCK);
  Register #(.width(16)) R6 (.D(DATA), .en(decoder_1_out6), .clk(not_7_out), .Q(R6_q), .clr(RESET));
  not not_7 (not_7_out, CLOCK);
  Register #(.width(16)) R7 (.D(DATA), .en(decoder_1_out7), .clk(not_8_out), .Q(R7_q), .clr(RESET));
  not not_8 (not_8_out, CLOCK);
  // Probe on R0_q
  // Probe on R1_q
  // Probe on R2_q
  // Probe on R3_q
  // Probe on R4_q
  // Probe on R5_q
  // Probe on R6_q
  // Probe on R7_q
  Multiplexer #(.select(3), .width(16)) multiplexer_1 (
    .in0(R0_q), .in1(R1_q), .in2(R2_q), .in3(R3_q), .in4(R4_q), .in5(R5_q), .in6(R6_q), .in7(R7_q),
    .out(DATA_RA_OUT), .sel(RA_OUT));
  Multiplexer #(.select(3), .width(16)) multiplexer_2 (
    .in0(R0_q), .in1(R1_q), .in2(R2_q), .in3(R3_q), .in4(R4_q), .in5(R5_q), .in6(R6_q), .in7(R7_q),
    .out(DATA_RB_OUT), .sel(RB_OUT));

  // Notes on the sheet:
  //   R0
  //   R1
  //   R2
  //   R3
  //   R4
  //   R5
  //   R6
  //   R7
endmodule

module INSTRUCTION_REG_MAIN (
  input  [15:0] DATA_IN,
  input  ENABLE,
  input  CLOCK,
  input  RESET,
  output [15:0] DATA_OUT
);

  Register #(.trigger("high"), .width(16)) register_1 (
    .D(DATA_IN), .en(ENABLE), .clk(CLOCK), .Q(DATA_OUT), .clr(RESET));

  // Notes on the sheet:
  //   INSTRUCTION REGISTER MAIN 16 bits
endmodule

module INSTRUCTION_REG_EXT (
  input  [15:0] DATA_IN,
  input  ENABLE,
  input  CLOCK,
  input  RESET,
  output [15:0] DATA_OUT
);

  Register #(.trigger("high"), .width(16)) register_1 (
    .D(DATA_IN), .en(ENABLE), .clk(CLOCK), .Q(DATA_OUT), .clr(RESET));

  // Notes on the sheet:
  //   INSTRUCTION REGISTER EXT 16 bits (Used for data : adresses, immediates, offsets)
endmodule

module PROGRAM_COUNTER (
  input  [15:0] PC_DATA,
  input  PC_Load,
  input  CLOCK,
  input  RESET,
  output [15:0] PC_Out
);

  wire [15:0] adder_1_out, multiplexer_1_out;

  Adder #(.width(16)) adder_1 (.a(PC_Out), .b(16'h1), .out(adder_1_out));  // open: cin, cout
  Multiplexer #(.width(16)) multiplexer_1 (.in0(adder_1_out), .in1(PC_DATA), .out(multiplexer_1_out), .sel(PC_Load));
  Register #(.width(16)) register_1 (.D(multiplexer_1_out), .en(1'b1), .clk(CLOCK), .Q(PC_Out), .clr(RESET));
endmodule

module FLAGS_REG (
  input  IN_Z,
  input  IN_N,
  input  IN_C,
  input  IN_O,
  input  ENABLE,
  input  CLOCK,
  input  RESET,
  output [3:0] OUT_DATA
);

  Register #(.width(4)) register_1 (.D({IN_O, IN_C, IN_N, IN_Z}), .en(ENABLE), .clk(CLOCK), .Q(OUT_DATA), .clr(RESET));

  // Notes on the sheet:
  //   FLAGS REGISTER (4bits) (bit 0 : equal to 0, bit 1 : negative, bit 2 : carry, bit 3 : overflow)
endmodule

module CONTROL_UNIT (
  input  [2:0] OpCode,
  input  [3:0] SubOpCode,
  input  [8:0] OpData,
  input  [3:0] FLAGS,
  output [5:0] ALU_Data,
  output RegWrite,
  output [2:0] SrcRB,
  output [2:0] SrcRA,
  output [2:0] DstR,
  output IsNextExt,
  output FlagsWrite,
  output MemWrite,
  output ContainsAddress,
  output PC_Load,
  output SP_POP,
  output SP_CHANGE,
  output JSR,
  output RTS,
  output REG_IS_ADR,
  output HALT,
  output USE_IN,
  output IO_SPACE,
  output [1:0] IO_PORT
);

  wire and_1_out, COMP_EXT, comparator_1_eq, comparator_2_eq, comparator_3_eq, comparator_4_eq,
       comparator_5_eq, comparator_6_eq, comparator_7_eq, comparator_8_eq, COMPM_SEL, IO_NB0, IO_WR,
       multiplexer_1_out, multiplexer_2_out, multiplexer_3_out, multiplexer_4_out, multiplexer_5_out,
       multiplexer_6_out, multiplexer_7_out, multiplexer_10_out, multiplexer_11_out, multiplexer_13_out,
       nor_1_out, not_1_out, not_2_out, not_3_out, or_1_out, or_2_out, xnor_1_out, xor_1_out;

  xnor xnor_1 (xnor_1_out, FLAGS[3], FLAGS[1]);
  and and_1 (and_1_out, xnor_1_out, not_1_out);
  not not_1 (not_1_out, FLAGS[0]);
  xor xor_1 (xor_1_out, FLAGS[3], FLAGS[1]);
  or or_1 (or_1_out, FLAGS[0], xor_1_out);
  nor nor_1 (nor_1_out, FLAGS[2], FLAGS[0]);
  Multiplexer #(.select(4)) multiplexer_1 (
    .in0(1'b1), .in1(1'b1), .in2(1'b0), .in3(1'b0), .in4(1'b0), .in5(1'b0), .in6(1'b0), .in7(1'b0),
    .in8(1'b0), .in9(1'b0), .in10(1'b0), .in11(1'b0), .in12(1'b0), .in13(1'b0), .in14(1'b0), .in15(1'b0),
    .out(multiplexer_1_out), .sel(SubOpCode));
  or or_2 (or_2_out, FLAGS[2], FLAGS[0]);
  not not_2 (not_2_out, FLAGS[2]);
  Multiplexer #(.select(4)) multiplexer_2 (
    .in0(1'b0), .in1(1'b1), .in2(1'b0), .in3(1'b0), .in4(1'b0), .in5(1'b0), .in6(1'b0), .in7(1'b0),
    .in8(1'b0), .in9(1'b0), .in10(1'b0), .in11(1'b0), .in12(1'b0), .in13(1'b0), .in14(1'b0), .in15(1'b0),
    .out(multiplexer_2_out), .sel(SubOpCode));
  Multiplexer #(.select(4)) multiplexer_3 (
    .in0(1'b0), .in1(1'b0), .in2(1'b0), .in3(1'b0), .in4(1'b0), .in5(1'b0), .in6(1'b0), .in7(1'b0),
    .in8(1'b1), .in9(1'b1), .in10(1'b1), .in11(1'b0), .out(multiplexer_3_out), .sel(SubOpCode));  // open: in12, in13, in14, in15
  Multiplexer #(.select(4)) multiplexer_4 (
    .in0(1'b0), .in1(1'b1), .in2(1'b1), .in3(1'b0), .in4(1'b0), .in5(1'b1), .in6(1'b0), .in7(1'b0),
    .in8(1'b0), .in9(1'b0), .in10(1'b0), .in11(1'b0), .in12(1'b0), .in13(1'b0), .in14(1'b0), .in15(1'b0),
    .out(multiplexer_4_out), .sel(SubOpCode));
  not not_3 (not_3_out, FLAGS[0]);
  Multiplexer #(.select(4)) multiplexer_5 (
    .in0(1'b1), .in1(FLAGS[0]), .in2(not_3_out), .in3(FLAGS[2]), .in4(or_2_out), .in5(nor_1_out),
    .in6(not_2_out), .in7(xor_1_out), .in8(or_1_out), .in9(and_1_out), .in10(xnor_1_out), .in11(1'b1),
    .in12(1'b0), .in13(1'b0), .in14(1'b0), .in15(1'b0), .out(multiplexer_5_out), .sel(SubOpCode));
  Multiplexer #(.select(4)) multiplexer_6 (
    .in0(1'b0), .in1(1'b0), .in2(1'b0), .in3(1'b0), .in4(1'b0), .in5(1'b0), .in6(1'b0), .in7(1'b0),
    .in8(1'b0), .in9(1'b0), .in10(1'b0), .in11(1'b1), .in12(1'b1), .in13(1'b0), .in14(1'b0), .in15(1'b0),
    .out(multiplexer_6_out), .sel(SubOpCode));
  Multiplexer #(.select(4)) multiplexer_7 (
    .in0(1'b0), .in1(1'b1), .in2(1'b0), .in3(1'b0), .in4(1'b0), .in5(1'b0), .in6(1'b0), .in7(1'b0),
    .in8(1'b0), .in9(1'b0), .in10(1'b0), .in11(1'b0), .in12(1'b0), .in13(1'b0), .in14(1'b0), .in15(1'b0),
    .out(multiplexer_7_out), .sel(SubOpCode));
  Multiplexer #(.select(3)) multiplexer_8 (
    .in0(1'b0), .in1(multiplexer_3_out), .in2(1'b0), .in3(1'b0), .in4(1'b0), .in5(1'b0), .in6(1'b0),
    .in7(1'b0), .out(FlagsWrite), .sel(OpCode));
  Multiplexer #(.select(3)) multiplexer_9 (
    .in0(1'b0), .in1(1'b0), .in2(1'b0), .in3(multiplexer_4_out), .in4(1'b0), .in5(1'b0), .in6(1'b0),
    .in7(IO_WR), .out(MemWrite), .sel(OpCode));
  Multiplexer #(.select(4)) multiplexer_10 (
    .in0(1'b0), .in1(1'b0), .in2(1'b0), .in3(1'b0), .in4(1'b0), .in5(1'b0), .in6(1'b0), .in7(1'b0),
    .in8(1'b0), .in9(1'b0), .in10(1'b0), .in11(1'b0), .in12(1'b1), .in13(1'b0), .in14(1'b0), .in15(1'b0),
    .out(multiplexer_10_out), .sel(SubOpCode));
  not not_4 (IO_NB0, IO_PORT[0]);
  Comparator #(.width(3)) comparator_1 (.a(OpCode), .b(3'b100), .eq(comparator_1_eq));  // open: gt, lt
  Comparator #(.width(4)) comparator_2 (.a(SubOpCode), .b(4'b1011), .eq(comparator_2_eq));  // open: gt, lt
  Comparator #(.width(3)) comparator_3 (.a(OpCode), .b(3'b100), .eq(comparator_3_eq));  // open: gt, lt
  Comparator #(.width(4)) comparator_4 (.a(SubOpCode), .b(4'b1100), .eq(comparator_4_eq));  // open: gt, lt
  Multiplexer #(.select(4)) multiplexer_11 (
    .in0(1'b0), .in1(1'b0), .in2(1'b1), .in3(1'b1), .in4(1'b1), .in5(1'b1), .in6(1'b0), .in7(1'b0),
    .in8(1'b0), .in9(1'b0), .in10(1'b0), .in11(1'b0), .in12(1'b0), .in13(1'b0), .in14(1'b0), .in15(1'b0),
    .out(multiplexer_11_out), .sel(SubOpCode));
  Comparator #(.width(3)) comparator_5 (.a(OpCode), .b(3'b111), .eq(comparator_5_eq));  // open: gt, lt
  Comparator #(.width(4)) comparator_6 (.a(SubOpCode), .b(4'b0000), .eq(comparator_6_eq));  // open: gt, lt
  xor xor_2 (IO_SPACE, IO_PORT[0], IO_PORT[1]);
  Comparator #(.width(4)) comparator_7 (.a(SubOpCode), .b(4'b0000), .eq(comparator_7_eq));  // open: gt, lt
  Multiplexer #(.select(3)) multiplexer_12 (
    .in0(1'b0), .in1(COMP_EXT), .in2(comparator_7_eq), .in3(multiplexer_1_out), .in4(1'b1),
    .in5(multiplexer_7_out), .in6(1'b0), .in7(IO_SPACE), .out(IsNextExt), .sel(OpCode));
  Multiplexer #(.select(4)) multiplexer_13 (
    .in0(1'b0), .in1(1'b1), .in2(1'b0), .in3(1'b0), .in4(1'b0), .in5(1'b0), .in6(1'b0), .in7(1'b0),
    .in8(1'b0), .in9(1'b0), .in10(1'b0), .in11(1'b0), .in12(1'b0), .in13(1'b0), .in14(1'b0), .in15(1'b0),
    .out(multiplexer_13_out), .sel(SubOpCode));
  Multiplexer #(.select(3)) multiplexer_14 (
    .in0(1'b0), .in1(1'b0), .in2(1'b0), .in3(multiplexer_11_out), .in4(1'b0), .in5(1'b0), .in6(1'b0),
    .in7(1'b0), .out(REG_IS_ADR), .sel(OpCode));
  Multiplexer #(.select(3)) multiplexer_15 (
    .in0(1'b0), .in1(COMPM_SEL), .in2(1'b0), .in3(1'b1), .in4(multiplexer_5_out), .in5(multiplexer_2_out),
    .in6(1'b0), .in7(IO_SPACE), .out(ContainsAddress), .sel(OpCode));
  Multiplexer #(.select(3)) multiplexer_16 (
    .in0(1'b0), .in1(1'b0), .in2(1'b0), .in3(1'b0), .in4(1'b1), .in5(1'b0), .in6(1'b0), .in7(1'b0),
    .out(PC_Load), .sel(OpCode));
  and and_2 (JSR, comparator_1_eq, comparator_2_eq);
  and and_3 (RTS, comparator_3_eq, comparator_4_eq);
  and and_4 (HALT, comparator_5_eq, comparator_6_eq);
  Multiplexer #(.select(3)) multiplexer_17 (
    .in0(1'b0), .in1(1'b0), .in2(1'b0), .in3(1'b0), .in4(multiplexer_10_out), .in5(multiplexer_13_out),
    .in6(1'b0), .in7(1'b0), .out(SP_POP), .sel(OpCode));
  Multiplexer #(.select(3)) multiplexer_18 (
    .in0(1'b0), .in1(1'b0), .in2(1'b0), .in3(1'b0), .in4(multiplexer_6_out), .in5(1'b1), .in6(1'b0),
    .in7(1'b0), .out(SP_CHANGE), .sel(OpCode));
  and and_5 (IO_WR, IO_PORT[1], IO_NB0);
  Comparator #(.width(4)) comparator_8 (.a(SubOpCode), .b(4'b1000), .eq(comparator_8_eq));  // open: gt, lt
  Comparator #(.width(4)) comparator_9 (.a(SubOpCode), .b(4'b1001), .eq(COMPM_SEL));  // open: gt, lt
  ROM #(.addrWidth(7), .dataWidth(10)) rom_1 (.addr({OpCode, SubOpCode}), .data({IO_PORT, USE_IN, RegWrite, ALU_Data}));
  or or_3 (COMP_EXT, comparator_8_eq, COMPM_SEL);

  assign DstR = OpData[8:6];
  assign SrcRA = OpData[5:3];
  assign SrcRB = OpData[2:0];

  // Other names for the same wires on the sheet: DEC_ALU[5:0] = ALU_Data; DEC_REGW = RegWrite; DEC_USE_IN = USE_IN;
  //   DEC_IO_PORT[1:0] = IO_PORT; IO_B0 = IO_PORT[0]; IO_B1 = IO_PORT[1]

  // Notes on the sheet:
  //   UPPER BIT IS : ENABLE/DISABLE ALU, LOWER 5 BITS ARE : ALUOpCode
  //   IO_MODE : 00 none, 01 IN, 10 OUT, 11 RAND. IN and OUT are 2 words : word 2 is the IO port address
  //   IO_SPACE (IN or OUT) sets ContainsAddress and IsNextExt, IO_WR (OUT) sets MemWrite : same timing as LOAD / STORE
  //   ENABLE WRITING TO FLAGS REGISTER
  //   ENABLE WRITING TO GP REGISTER (DstR)
  //   INDICATES THAT THE NEXT WORD IS AN EXTENSION OF THIS INSTRUCTION
  //   contents of rom_1 (hex, n*v repeats v):
  //   0 61 62 63 64 65 66 67 68 69 60 6d 6e 6c 6f 70 71 72 73 74 75 76 78 7a 2a 2a 2a 6b 4*0 40 77 15*40 0
  //   0 40 78 38 27*0 40 31*0 140 200 3c0
  //   DECODE ROM : address = OpCode:SubOpCode, data = IO_PORT(2) USE_IN RegWrite ALU_Data(6)
endmodule

module IO_PORTS (
  input  RESET,
  input  [15:0] IO_PORT_SELECT,
  input  IO_IN_OR_OUT,
  input  [15:0] IO_DATA_IN,
  input  CLOCK_SIGNAL,
  output [15:0] IO_DATA_OUT
);

  wire and_1_out, and_2_out, and_3_out, IO_VALID, or_1_out, or_2_out, or_3_out, SEL0, SEL1, SEL2, SEL3;
  wire [1:0] IO_SEL;
  wire [15:0] IO_DATA_MUXED, IO_PORT_0_p3, IO_PORT_1_p3, IO_PORT_2_p3, RAND_OUT;

  Comparator #(.width(16)) comparator_1 (.a(IO_PORT_SELECT), .b(16'h1000), .eq(SEL0));  // open: gt, lt
  Comparator #(.width(16)) comparator_2 (.a(IO_PORT_SELECT), .b(16'h1001), .eq(SEL1));  // open: gt, lt
  Comparator #(.width(16)) comparator_3 (.a(IO_PORT_SELECT), .b(16'h1002), .eq(SEL2));  // open: gt, lt
  Comparator #(.width(16)) comparator_4 (.a(IO_PORT_SELECT), .b(16'h1003), .eq(SEL3));  // open: gt, lt
  and and_1 (and_1_out, IO_IN_OR_OUT, SEL0);
  and and_2 (and_2_out, IO_IN_OR_OUT, SEL1);
  and and_3 (and_3_out, IO_IN_OR_OUT, SEL2);
  Random #(.width(16)) random_1 (.clk(CLOCK_SIGNAL), .out(RAND_OUT));  // open: clr, next
  or or_1 (or_1_out, and_1_out, RESET);
  or or_2 (or_2_out, and_2_out, RESET);
  or or_3 (or_3_out, and_3_out, RESET);
  // PortIO #(.number(16)) IO_PORT_0: pin names not known; wires that end beside it: or_1_out, IO_DATA_IN, IO_PORT_0_p3
  // PortIO #(.number(16)) IO_PORT_1: pin names not known; wires that end beside it: or_2_out, IO_DATA_IN, IO_PORT_1_p3
  // PortIO #(.number(16)) IO_PORT_2: pin names not known; wires that end beside it: or_3_out, IO_DATA_IN, IO_PORT_2_p3
  or or_4 (IO_SEL[0], SEL1, SEL3);
  or or_5 (IO_SEL[1], SEL2, SEL3);
  or or_6 (IO_VALID, SEL0, SEL1, SEL2, SEL3);
  Multiplexer #(.select(2), .width(16)) multiplexer_1 (
    .in0(IO_PORT_0_p3), .in1(IO_PORT_1_p3), .in2(IO_PORT_2_p3), .in3(RAND_OUT), .out(IO_DATA_MUXED),
    .sel(IO_SEL));
  Multiplexer #(.width(16)) multiplexer_2 (.in0({16{1'b0}}), .in1(IO_DATA_MUXED), .out(IO_DATA_OUT), .sel(IO_VALID));

  // Other names for the same wires on the sheet: IO_IN_OUT = IO_IN_OR_OUT; IO_PORT[15:0] = IO_PORT_SELECT;
  //   IO_SEL_B0 = IO_SEL[0]; IO_SEL_B1 = IO_SEL[1]

  // Notes on the sheet:
  //   RAND : random generator, IO address 0x1003 (the RAND instruction reads it directly)
  //   IO address map : IO_PORT_0 = 0x1000, IO_PORT_1 = 0x1001, IO_PORT_2 = 0x1002, RAND = 0x1003. Other addresses read 0
endmodule

module GPU (
  input  [15:0] RAM_ADRESS,
  output SCREEN_WRITE_ENABLE,
  output [6:0] SCREEN_X,
  output [6:0] SCREEN_Y
);

  wire comparator_1_eq, comparator_1_gt, comparator_2_lt, comparator_3_eq, or_1_out;
  wire [6:0] divider_1_rem;

  Comparator #(.mode("unsigned"), .width(16)) comparator_1 (
    .a(RAM_ADRESS), .b(16'h8000), .gt(comparator_1_gt), .eq(comparator_1_eq));  // open: lt
  Comparator #(.mode("unsigned"), .width(16)) comparator_2 (
    .a(RAM_ADRESS), .b(16'hc000), .lt(comparator_2_lt));  // open: gt, eq
  or or_1 (or_1_out, comparator_1_gt, comparator_1_eq);
  and and_1 (SCREEN_WRITE_ENABLE, or_1_out, comparator_2_lt);
  // Probe on RAM_ADRESS
  Divider #(.width(7)) divider_1 (.a(RAM_ADRESS[6:0]), .b({7{1'b1}}), .rem(divider_1_rem));  // open: out, upper
  Comparator #(.mode("unsigned"), .width(7)) comparator_3 (
    .a(RAM_ADRESS[6:0]), .b({7{1'b1}}), .eq(comparator_3_eq));  // open: gt, lt
  Multiplexer #(.width(7)) multiplexer_1 (.in0(divider_1_rem), .in1({7{1'b1}}), .out(SCREEN_X), .sel(comparator_3_eq));

  assign SCREEN_Y = RAM_ADRESS[13:7];
endmodule

module RAM_MODULE (
  input  RESET,
  input  [15:0] RAM_ADRESS_IN,
  input  WRITE_ENABLE,
  input  RAM_CLOCK,
  input  [15:0] RAM_DATA_IN,
  output [15:0] RAM_ADRESS_OUT,
  output [15:0] RAM_DATA_OUT,
  output [15:0] RAM_WRITTEN_DATA
);

  wire button_1_out, multiplexer_1_out, multiplexer_2_out;
  wire [15:0] dipswitch_1_sw16, dipswitch_2_sw16;

  DipSwitch #(.number(16)) dipswitch_1 (
    .sw1(dipswitch_1_sw16[15]), .sw2(dipswitch_1_sw16[14]), .sw3(dipswitch_1_sw16[13]),
    .sw4(dipswitch_1_sw16[12]), .sw5(dipswitch_1_sw16[11]), .sw6(dipswitch_1_sw16[10]),
    .sw7(dipswitch_1_sw16[9]), .sw8(dipswitch_1_sw16[8]), .sw9(dipswitch_1_sw16[7]),
    .sw10(dipswitch_1_sw16[6]), .sw11(dipswitch_1_sw16[5]), .sw12(dipswitch_1_sw16[4]),
    .sw13(dipswitch_1_sw16[3]), .sw14(dipswitch_1_sw16[2]), .sw15(dipswitch_1_sw16[1]),
    .sw16(dipswitch_1_sw16[0]));
  Multiplexer multiplexer_1 (.in0(WRITE_ENABLE), .in1(1'b1), .out(multiplexer_1_out), .sel(button_1_out));
  DipSwitch #(.number(16)) dipswitch_2 (
    .sw1(dipswitch_2_sw16[15]), .sw2(dipswitch_2_sw16[14]), .sw3(dipswitch_2_sw16[13]),
    .sw4(dipswitch_2_sw16[12]), .sw5(dipswitch_2_sw16[11]), .sw6(dipswitch_2_sw16[10]),
    .sw7(dipswitch_2_sw16[9]), .sw8(dipswitch_2_sw16[8]), .sw9(dipswitch_2_sw16[7]),
    .sw10(dipswitch_2_sw16[6]), .sw11(dipswitch_2_sw16[5]), .sw12(dipswitch_2_sw16[4]),
    .sw13(dipswitch_2_sw16[3]), .sw14(dipswitch_2_sw16[2]), .sw15(dipswitch_2_sw16[1]),
    .sw16(dipswitch_2_sw16[0]));
  Multiplexer multiplexer_2 (.in0(RAM_CLOCK), .in1(1'b1), .out(multiplexer_2_out), .sel(button_1_out));
  Multiplexer #(.width(16)) multiplexer_3 (
    .in0(RAM_ADRESS_IN), .in1(dipswitch_1_sw16), .out(RAM_ADRESS_OUT), .sel(button_1_out));
  Multiplexer #(.width(16)) multiplexer_4 (
    .in0(RAM_DATA_IN), .in1(dipswitch_2_sw16), .out(RAM_WRITTEN_DATA), .sel(button_1_out));
  Button button_1 (.out(button_1_out));
  RAM #(.addrWidth(16), .clearpin("true"), .dataWidth(16), .enables("line"), .\type ("nonvolatile")) RAM_1Mbit (
    .addr(RAM_ADRESS_OUT), .we(multiplexer_1_out), .clk(multiplexer_2_out), .din(RAM_WRITTEN_DATA),
    .dout(RAM_DATA_OUT), .clr(RESET));

  // Notes on the sheet:
  //   ADDRESS
  //   DATA
  //   WRITE
  //   NOTE : MOST MODERN PARALLEL 64Kx16
  //   SRAMs AREN'T ASYNCHRONOUS,
  //    SO TO IMPLEMENT THE PROCESSOR IRL,
  //   THE RAM NEEDS A LITTLE BIT OF TWEAKING
endmodule
